// Logisim project alu.circ as structural Verilog: 1 circuit, main circuit main
module main (
  input  [31:0] X,
  input  [31:0] Y,
  input  [3:0] Switch,
  output Signed_Overflow,
  output Equal,
  output [31:0] Result,
  output [31:0] Result_2
);

  wire add_overflow, add_switch, comparator_2_lt, comparator_3_lt, comparator_4_eq, comparator_5_eq,
       divu_switch, multiplexer_1_out, multiplexer_2_out, multiplexer_7_out, multiplexer_9_out, multu_switch,
       not_1_out, not_2_out, not_3_out, sub_overflow, sub_switch;
  wire [4:0] bit_extender_1_out, bit_extender_2_out, bit_extender_3_out;
  wire [31:0] add_out, addu_out, and_out, divu_out, divu_rem, multiplexer_5_out, multiplexer_6_out,
       multu_out, multu_upperbit, or_out, sll_out, slt_out, sltu_out, sra_out, srl_out, sub_out, subu_out;

  Comparator #(.width(32)) comparator_1 (.a(X), .b(Y), .eq(Equal));  // open: gt, lt
  Multiplexer multiplexer_1 (.in0(1'b0), .in1(add_overflow), .out(multiplexer_1_out), .sel(add_switch));  // open: en
  Multiplexer multiplexer_2 (.in0(1'b0), .in1(sub_overflow), .out(multiplexer_2_out), .sel(sub_switch));  // open: en
  Bit_Extender #(.in_width(32), .out_width(5)) bit_extender_1 (.in(Y), .out(bit_extender_1_out));
  Bit_Extender #(.in_width(32), .out_width(5)) bit_extender_2 (.in(Y), .out(bit_extender_2_out));
  Bit_Extender #(.in_width(32), .out_width(5)) bit_extender_3 (.in(Y), .out(bit_extender_3_out));
  Multiplexer multiplexer_3 (
    .in0(multiplexer_1_out), .in1(multiplexer_2_out), .out(Signed_Overflow), .sel(sub_switch));  // open: en
  Shifter #(.width(32)) shifter_1 (.in(X), .\dist (bit_extender_1_out), .out(sll_out));
  Shifter #(.width(32), .shift("lr")) shifter_2 (.in(X), .\dist (bit_extender_2_out), .out(srl_out));
  Shifter #(.width(32), .shift("ar")) shifter_3 (.in(X), .\dist (bit_extender_3_out), .out(sra_out));
  Multiplier #(.width(32)) multiplier_1 (.a(X), .b(Y), .out(multu_out), .cout(multu_upperbit));  // open: cin
  Divider #(.width(32)) divider_1 (.a(X), .b(Y), .out(divu_out), .rem(divu_rem));  // open: upper
  Adder #(.width(32)) adder_1 (.a(X), .b(Y), .out(addu_out));  // open: cin, cout
  Subtractor #(.width(32)) subtractor_1 (.a(X), .b(Y), .out(subu_out));  // open: bin, bout
  assign and_out = X & Y;  // AND_Gate and, 32 bits wide
  assign or_out = X | Y;  // OR_Gate or, 32 bits wide
  Comparator #(.width(32)) comparator_2 (.a(X), .b(Y), .lt(comparator_2_lt));  // open: gt, eq
  assign slt_out = {{31{1'b0}}, comparator_2_lt};  // Bit_Extender bit_extender_4
  Comparator #(.width(32), .mode("unsigned")) comparator_3 (.a(X), .b(Y), .lt(comparator_3_lt));  // open: gt, eq
  assign sltu_out = {{31{1'b0}}, comparator_3_lt};  // Bit_Extender bit_extender_5
  Comparator #(.width(1)) comparator_4 (.a(Y[31]), .b(X[31]), .eq(comparator_4_eq));  // open: gt, lt
  Comparator #(.width(1)) comparator_5 (.a(Y[31]), .b(X[31]), .eq(comparator_5_eq));  // open: gt, lt
  Adder #(.width(32)) adder_2 (.a(X), .b(Y), .out(add_out));  // open: cin, cout
  not not_1 (not_1_out, sub_out[31]);
  not not_2 (not_2_out, comparator_4_eq);
  Subtractor #(.width(32)) subtractor_2 (.a(X), .b(Y), .out(sub_out));  // open: bin, bout
  Multiplexer #(.select(4), .width(32)) multiplexer_4 (
    .in0(sll_out), .in1(srl_out), .in2(sra_out), .in3(multu_out), .in4(divu_out), .in5(add_out),
    .in7(addu_out), .in10(sub_out), .in11(subu_out), .in12(and_out), .in13(or_out), .in14(slt_out),
    .in15(sltu_out), .out(Result), .sel(Switch));  // open: in6, in8, in9, en
  Comparator #(.width(4)) comparator_6 (.a(4'b0101), .b(Switch), .eq(add_switch));  // open: gt, lt
  Comparator #(.width(4)) comparator_7 (.a(4'b0111), .b(Switch), .eq(sub_switch));  // open: gt, lt
  Multiplexer #(.width(32)) multiplexer_5 (
    .in0({32{1'b0}}), .in1(multu_upperbit), .out(multiplexer_5_out), .sel(multu_switch));  // open: en
  Multiplexer #(.width(32)) multiplexer_6 (
    .in0({32{1'b0}}), .in1(divu_rem), .out(multiplexer_6_out), .sel(divu_switch));  // open: en
  not not_3 (not_3_out, add_out[31]);
  Multiplexer multiplexer_7 (.in0(not_1_out), .in1(Y[31]), .out(multiplexer_7_out), .sel(not_2_out));  // open: en
  Multiplexer #(.width(32)) multiplexer_8 (
    .in0(multiplexer_5_out), .in1(multiplexer_6_out), .out(Result_2), .sel(divu_switch));  // open: en
  Multiplexer multiplexer_9 (
    .in0(add_out[31]), .in1(X[31]), .out(multiplexer_9_out), .sel(comparator_5_eq));  // open: en
  Comparator #(.width(1)) comparator_8 (.a(multiplexer_7_out), .b(sub_out[31]), .eq(sub_overflow));  // open: gt, lt
  Comparator #(.width(4)) comparator_9 (.a(4'b0011), .b(Switch), .eq(multu_switch));  // open: gt, lt
  Comparator #(.width(4)) comparator_10 (.a(4'b0100), .b(Switch), .eq(divu_switch));  // open: gt, lt
  Comparator #(.width(1)) comparator_11 (.a(multiplexer_9_out), .b(not_3_out), .eq(add_overflow));  // open: gt, lt

  // Other names for the same wires on the sheet: overflow = Signed_Overflow; S[3:0] = Switch

  // Notes on the sheet:
  //   INPUTS to your circuit
  //   DON'T CHANGE THE LOCATIONS OF THE INPUTS AND OUTPUTS!
  //   OUTPUTS from your circuit
endmodule
