// Logisim project cpu3.circ as structural Verilog: 2 circuits, main circuit main
module main (
  input  [31:0] INSTRUCTION,
  input  CLOCK,
  output [31:0] FETCH_ADDRESS,
  output [31:0] s0_Value,
  output [31:0] s1_Value,
  output [31:0] s2_Value,
  output [31:0] ra_Value,
  output [31:0] HI_Value,
  output [31:0] LO_Value,
  output [5:0] To_Instr_Mem
);

  wire ALUSrc, and_2_out, and_3_out, beq, beqal, bne, Branch, eq, ExtOp, j, jal, jr, Jump, lui,
       main_2_signed_overflow, MEM_p1, MemToReg, MemWrite, not_1_out, or_2_out, or_3_out, RegDest, shift,
       write_en;
  wire [2:0] OP_Unit;
  wire [3:0] ALUCtr;
  wire [4:0] multiplexer_4_out;
  wire [5:0] funct;
  wire [15:6] immediate;
  wire [25:16] INSTRUCTION_t;
  wire [31:0] adder_1_out, and_1_out, bit_extender_1_out, bit_extender_2_out, bit_extender_3_out,
       bit_extender_4_out, bit_extender_5_out, Extend_Immediate, hi_out, lo_out, main_1_read_data_1,
       main_1_read_data_2, MEM_p7, multiplexer_1_out, multiplexer_2_out, multiplexer_3_out,
       multiplexer_6_out, multiplexer_7_out, multiplexer_8_out, multiplexer_9_out, or_1_out, PC_Exit,
       PC_Increment, shifter_1_out, shifter_2_out, shifter_3_out, write_data;

  assign bit_extender_1_out = {{6{1'b0}}, {INSTRUCTION_t, immediate, funct}};  // Bit_Extender bit_extender_1
  Shifter #(.width(32)) shifter_1 (.in(Extend_Immediate), .\dist (5'b00010), .out(shifter_1_out));
  control control_1 (
    .opcode(To_Instr_Mem), .funct(funct), .RegDest(RegDest), .ALUSrc(ALUSrc), .beq(beq), .beqal(beqal),
    .ALUCtr(ALUCtr), .bne(bne), .j(j), .jal(jal), .MemToReg(MemToReg), .lui(lui), .MemWrite(MemWrite),
    .jr(jr), .write_en(write_en), .ExtOp(ExtOp), .OPUnit(OP_Unit), .shift(shift));
  Shifter #(.width(32)) shifter_2 (.in(bit_extender_1_out), .\dist (5'b00010), .out(shifter_2_out));
  assign or_1_out = shifter_2_out | and_1_out;  // OR_Gate or_1, 32 bits wide
  assign and_1_out = PC_Increment & 32'hf0000000;  // AND_Gate and_1, 32 bits wide
  Multiplexer #(.width(32)) multiplexer_1 (
    .in0(PC_Increment), .in1(adder_1_out), .out(multiplexer_1_out), .sel(Branch));  // open: en
  Adder #(.width(32)) adder_1 (.a(PC_Exit), .b(shifter_1_out), .out(adder_1_out));  // open: cin, cout
  Multiplexer #(.width(32)) multiplexer_2 (
    .in0(or_1_out), .in1(multiplexer_1_out), .out(multiplexer_2_out), .sel(Jump));  // open: en
  Register #(.width(32)) PC (.D(multiplexer_2_out), .Q(FETCH_ADDRESS), .clk(CLOCK));  // open: en, clr
  Adder #(.width(32)) adder_2 (.a(FETCH_ADDRESS), .b(32'h4), .out(PC_Increment));  // open: cin, cout
  Multiplexer #(.width(32)) multiplexer_3 (
    .in0(INSTRUCTION), .in1({32{1'b0}}), .out(multiplexer_3_out), .sel(or_2_out));  // open: en
  or or_2 (or_2_out, Branch, Jump);
  Register #(.width(32)) Pipeline (
    .D(multiplexer_3_out), .Q({To_Instr_Mem, INSTRUCTION_t, immediate, funct}), .clk(CLOCK));  // open: en, clr
  Multiplexer #(.width(5)) multiplexer_4 (
    .in0(INSTRUCTION_t[20:16]), .in1(immediate[15:11]), .out(multiplexer_4_out), .sel(RegDest));  // open: en
  not not_1 (not_1_out, eq);
  and and_2 (and_2_out, not_1_out, bne);
  and and_3 (and_3_out, eq, or_3_out);
  or or_3 (or_3_out, beq, beqal);
  or or_4 (Jump, j, jal);
  regfile_main main_1 (
    .Read_Register_1(INSTRUCTION_t[25:21]), .Read_Register_2(INSTRUCTION_t[20:16]),
    .Write_Register(multiplexer_4_out), .Write_Data(write_data), .Write_Enable(write_en), .Clock(CLOCK),
    .Read_Data_1(main_1_read_data_1), .Read_Data_2(main_1_read_data_2), .s0_Value(s0_Value),
    .s1_Value(s1_Value), .s2_Value(s2_Value), .ra_Value(ra_Value));
  or or_5 (Branch, and_2_out, j, jal, jr, and_3_out);
  assign bit_extender_2_out = {{16{immediate[15]}}, {immediate, funct}};  // Bit_Extender bit_extender_2
  assign bit_extender_3_out = {{16{1'b0}}, {immediate, funct}};  // Bit_Extender bit_extender_3
  Multiplexer #(.width(32)) multiplexer_5 (
    .in0(bit_extender_2_out), .in1(bit_extender_3_out), .out(Extend_Immediate), .sel(ExtOp));  // open: en
  Multiplexer #(.width(32)) multiplexer_6 (
    .in0(main_1_read_data_1), .in1(main_1_read_data_2), .out(multiplexer_6_out), .sel(shift));  // open: en
  Multiplexer #(.width(32)) multiplexer_7 (
    .in0(main_1_read_data_2), .in1(Extend_Immediate), .out(multiplexer_7_out), .sel(ALUSrc));  // open: en
  Multiplexer #(.width(32)) multiplexer_8 (
    .in0(multiplexer_7_out), .in1(bit_extender_4_out), .out(multiplexer_8_out), .sel(shift));  // open: en
  assign bit_extender_4_out = {{27{1'b0}}, immediate[10:6]};  // Bit_Extender bit_extender_4
  LED signed_overflow (.in(main_2_signed_overflow));
  alu_main main_2 (
    .Switch(ALUCtr), .X(multiplexer_6_out), .Equal(eq), .Result(lo_out),
    .Signed_Overflow(main_2_signed_overflow), .Y(multiplexer_8_out), .Result_2(hi_out));
  assign bit_extender_5_out = {{16{1'b0}}, {immediate, funct}};  // Bit_Extender bit_extender_5
  Register #(.width(32)) HI (.D(hi_out), .Q(HI_Value), .clk(CLOCK));  // open: en, clr
  Register #(.width(32)) LO (.D(lo_out), .Q(LO_Value), .clk(CLOCK));  // open: en, clr
  Shifter #(.width(32)) shifter_3 (.in(bit_extender_5_out), .\dist (5'b10000), .out(shifter_3_out));
  Multiplexer #(.width(32)) multiplexer_9 (
    .in0(lo_out), .in1(shifter_3_out), .out(multiplexer_9_out), .sel(lui));  // open: en
  // mem_main MEM: pin names not known; wires that end beside it: MEM_p1, lo_out, main_1_read_data_2, MemWrite, CLOCK, OP_Unit, MEM_p7
  Multiplexer #(.width(32)) multiplexer_10 (
    .in0(multiplexer_9_out), .in1(MEM_p7), .out(write_data), .sel(MemToReg));  // open: en

  // Other names for the same wires on the sheet: clk = CLOCK; fetch_addr[31:0] = FETCH_ADDRESS; hi_t[31:0] = HI_Value;
  //   immediate[5:0] = funct; INSTRUCTION_t (some bits) = {To_Instr_Mem, immediate, funct};
  //   jump_address[25:0] = {INSTRUCTION_t, immediate, funct}; shamt[4:0] = immediate[10:6];
  //   rd[4:0] = immediate[15:11]; rt[4:0] = INSTRUCTION_t[20:16]; rs[4:0] = INSTRUCTION_t[25:21];
  //   opcode[5:0] = To_Instr_Mem; lo_t[31:0] = LO_Value; ra_t[31:0] = ra_Value; s0_t[31:0] = s0_Value;
  //   s1_t[31:0] = s1_Value; s2_t[31:0] = s2_Value

  // Notes on the sheet:
  //   Output
  //   Control Unit
  //   These are outputs/inputs from run.circ
  //   PC Logic
  //   Instruction Parsing
  //   Inputs
  //   These are DEBUG/TEST outputs from your circuit.
endmodule

module control (
  input  [5:0] opcode,
  input  [5:0] funct,
  output RegDest,
  output ALUSrc,
  output beq,
  output beqal,
  output [3:0] ALUCtr,
  output bne,
  output j,
  output jal,
  output MemToReg,
  output lui,
  output MemWrite,
  output jr,
  output write_en,
  output ExtOp,
  output [2:0] OPUnit,
  output shift
);

  wire comparator_25_eq, comparator_26_eq, comparator_27_eq, comparator_28_eq, comparator_29_eq,
       comparator_30_eq, comparator_31_eq, comparator_32_eq, comparator_33_eq, comparator_34_eq, is_addi,
       is_addiu, is_andi, is_jr, is_lb, is_lbu, is_lhu, is_lw, is_ori, is_sb, is_sh, is_sll, is_slti, is_sra,
       is_srl, is_sw, is_swinc, or_2_out, or_3_out, or_7_out, or_8_out, or_9_out, or_10_out, or_11_out;

  Comparator #(.width(6), .mode("unsigned")) comparator_1 (.a(6'b001000), .b(opcode), .eq(is_addi));  // open: gt, lt
  Comparator #(.width(6), .mode("unsigned")) comparator_2 (.a(6'b001001), .b(opcode), .eq(is_addiu));  // open: gt, lt
  Comparator #(.width(6), .mode("unsigned")) comparator_3 (.a(6'b001100), .b(opcode), .eq(is_andi));  // open: gt, lt
  Comparator #(.width(6), .mode("unsigned")) comparator_4 (.a(6'b000100), .b(opcode), .eq(beq));  // open: gt, lt
  Comparator #(.width(6), .mode("unsigned")) comparator_5 (.a(6'b010100), .b(opcode), .eq(beqal));  // open: gt, lt
  Comparator #(.width(6), .mode("unsigned")) comparator_6 (.a(6'b000101), .b(opcode), .eq(bne));  // open: gt, lt
  Comparator #(.width(6), .mode("unsigned")) comparator_7 (.a(6'b000010), .b(opcode), .eq(j));  // open: gt, lt
  Comparator #(.width(6), .mode("unsigned")) comparator_8 (.a(6'b000011), .b(opcode), .eq(jal));  // open: gt, lt
  Comparator #(.width(6), .mode("unsigned")) comparator_9 (.a(6'b100000), .b(opcode), .eq(is_lb));  // open: gt, lt
  Comparator #(.width(6), .mode("unsigned")) comparator_10 (.a(6'b100100), .b(opcode), .eq(is_lbu));  // open: gt, lt
  Comparator #(.width(6), .mode("unsigned")) comparator_11 (.a(6'b100101), .b(opcode), .eq(is_lhu));  // open: gt, lt
  Comparator #(.width(6), .mode("unsigned")) comparator_12 (.a(6'b001111), .b(opcode), .eq(lui));  // open: gt, lt
  Comparator #(.width(6), .mode("unsigned")) comparator_13 (.a(6'b100011), .b(opcode), .eq(is_lw));  // open: gt, lt
  Comparator #(.width(6), .mode("unsigned")) comparator_14 (.a(6'b001101), .b(opcode), .eq(is_ori));  // open: gt, lt
  Comparator #(.width(6), .mode("unsigned")) comparator_15 (.a(6'b001010), .b(opcode), .eq(is_slti));  // open: gt, lt
  Comparator #(.width(6), .mode("unsigned")) comparator_16 (.a(6'b101000), .b(opcode), .eq(is_sb));  // open: gt, lt
  Comparator #(.width(6), .mode("unsigned")) comparator_17 (.a(6'b101001), .b(opcode), .eq(is_sh));  // open: gt, lt
  Comparator #(.width(6), .mode("unsigned")) comparator_18 (.a(6'b101011), .b(opcode), .eq(is_sw));  // open: gt, lt
  Comparator #(.width(6), .mode("unsigned")) comparator_19 (.a(6'b101100), .b(opcode), .eq(is_swinc));  // open: gt, lt
  or or_1 (ExtOp, is_andi, is_ori);
  assign OPUnit = is_lbu ? 3'b000 : 3'bz;  // Controlled_Buffer controlled_buffer_1
  assign OPUnit = or_2_out ? 3'b001 : 3'bz;  // Controlled_Buffer controlled_buffer_2
  or or_2 (or_2_out, is_lb, is_sb);
  assign OPUnit = is_lhu ? 3'b010 : 3'bz;  // Controlled_Buffer controlled_buffer_3
  Comparator #(.width(6), .mode("unsigned")) comparator_20 (.a({6{1'b0}}), .b(opcode), .eq(RegDest));  // open: gt, lt
  and and_1 (jr, RegDest, is_jr);
  assign OPUnit = is_sh ? 3'b011 : 3'bz;  // Controlled_Buffer controlled_buffer_4
  assign OPUnit = or_3_out ? 3'b100 : 3'bz;  // Controlled_Buffer controlled_buffer_5
  or or_3 (or_3_out, is_lw, is_sw, is_swinc);
  or or_4 (MemWrite, is_sb, is_sh, is_sw, is_swinc);
  or or_5 (shift, is_sll, is_srl, is_sra);
  nor nor_1 (ALUSrc, RegDest, beq, beqal, bne);
  or or_6 (MemToReg, is_lb, is_lbu, is_lhu, is_lw);
  nor nor_2 (write_en, jr, j, is_sw, beq, bne, beqal, is_sb, is_sh);
  Comparator #(.width(6), .mode("unsigned")) comparator_21 (.a(6'b001000), .b(funct), .eq(is_jr));  // open: gt, lt
  Comparator #(.width(6), .mode("unsigned")) comparator_22 (.a({6{1'b0}}), .b(funct), .eq(is_sll));  // open: gt, lt
  Comparator #(.width(6), .mode("unsigned")) comparator_23 (.a(6'b000010), .b(funct), .eq(is_srl));  // open: gt, lt
  Comparator #(.width(6), .mode("unsigned")) comparator_24 (.a(6'b000011), .b(funct), .eq(is_sra));  // open: gt, lt
  Comparator #(.width(6), .mode("unsigned")) comparator_25 (
    .a(6'b011001), .b(funct), .eq(comparator_25_eq));  // open: gt, lt
  Comparator #(.width(6), .mode("unsigned")) comparator_26 (
    .a(6'b011011), .b(funct), .eq(comparator_26_eq));  // open: gt, lt
  Comparator #(.width(6), .mode("unsigned")) comparator_27 (
    .a(6'b100000), .b(funct), .eq(comparator_27_eq));  // open: gt, lt
  Comparator #(.width(6), .mode("unsigned")) comparator_28 (
    .a(6'b100010), .b(funct), .eq(comparator_28_eq));  // open: gt, lt
  Comparator #(.width(6), .mode("unsigned")) comparator_29 (
    .a(6'b100100), .b(funct), .eq(comparator_29_eq));  // open: gt, lt
  Comparator #(.width(6), .mode("unsigned")) comparator_30 (
    .a(6'b100101), .b(funct), .eq(comparator_30_eq));  // open: gt, lt
  Comparator #(.width(6), .mode("unsigned")) comparator_31 (
    .a(6'b101010), .b(funct), .eq(comparator_31_eq));  // open: gt, lt
  Comparator #(.width(6), .mode("unsigned")) comparator_32 (
    .a(6'b101011), .b(funct), .eq(comparator_32_eq));  // open: gt, lt
  Comparator #(.width(6), .mode("unsigned")) comparator_33 (
    .a(6'b100001), .b(funct), .eq(comparator_33_eq));  // open: gt, lt
  Comparator #(.width(6), .mode("unsigned")) comparator_34 (
    .a(6'b100011), .b(funct), .eq(comparator_34_eq));  // open: gt, lt
  assign ALUCtr = or_7_out ? 4'b0000 : 4'bz;  // Controlled_Buffer controlled_buffer_6
  or or_7 (or_7_out, lui, is_sll);
  assign ALUCtr = is_srl ? 4'b0001 : 4'bz;  // Controlled_Buffer controlled_buffer_7
  assign ALUCtr = is_sra ? 4'b0010 : 4'bz;  // Controlled_Buffer controlled_buffer_8
  assign ALUCtr = comparator_25_eq ? 4'b0011 : 4'bz;  // Controlled_Buffer controlled_buffer_9
  assign ALUCtr = comparator_26_eq ? 4'b0100 : 4'bz;  // Controlled_Buffer controlled_buffer_10
  assign ALUCtr = comparator_27_eq ? 4'b0101 : 4'bz;  // Controlled_Buffer controlled_buffer_11
  assign ALUCtr = comparator_28_eq ? 4'b0111 : 4'bz;  // Controlled_Buffer controlled_buffer_12
  assign ALUCtr = or_8_out ? 4'b1001 : 4'bz;  // Controlled_Buffer controlled_buffer_13
  or or_8 (or_8_out, is_andi, comparator_29_eq);
  assign ALUCtr = or_9_out ? 4'b1010 : 4'bz;  // Controlled_Buffer controlled_buffer_14
  or or_9 (or_9_out, is_ori, comparator_30_eq);
  assign ALUCtr = comparator_31_eq ? 4'b1011 : 4'bz;  // Controlled_Buffer controlled_buffer_15
  assign ALUCtr = comparator_32_eq ? 4'b1100 : 4'bz;  // Controlled_Buffer controlled_buffer_16
  assign ALUCtr = or_11_out ? 4'b0110 : 4'bz;  // Controlled_Buffer controlled_buffer_17
  assign ALUCtr = or_10_out ? 4'b1000 : 4'bz;  // Controlled_Buffer controlled_buffer_18
  or or_10 (or_10_out, comparator_34_eq, beq, beqal, bne);
  or or_11 (or_11_out, comparator_33_eq, is_lb, is_lbu, is_lhu, is_lw, is_sb, is_sh, is_sw, is_swinc, is_addi, is_addiu);

  // Other names for the same wires on the sheet: is_beq = beq; is_beqal = beqal; is_bne = bne; is_j = j; is_jal = jal;
  //   is_lui = lui; is_r_type = RegDest
endmodule
