// Logisim project regfile.circ as structural Verilog: 1 circuit, main circuit main
module main (
  input  [4:0] Read_Register_1,
  input  [4:0] Read_Register_2,
  input  [4:0] Write_Register,
  input  [31:0] Write_Data,
  input  Write_Enable,
  input  Clock,
  output [31:0] s0_Value,
  output [31:0] s1_Value,
  output [31:0] s2_Value,
  output [31:0] ra_Value,
  output [31:0] Read_Data_1,
  output [31:0] Read_Data_2
);

  wire reg_a0_write, reg_a1_write, reg_a2_write, reg_a3_write, reg_at_write, reg_fp_write, reg_gp_write,
       reg_k0_write, reg_k1_write, reg_ra_write, reg_s0_write, reg_s1_write, reg_s2_write, reg_s3_write,
       reg_s4_write, reg_s5_write, reg_s6_write, reg_s7_write, reg_sp_write, reg_t0_write, reg_t1_write,
       reg_t2_write, reg_t3_write, reg_t4_write, reg_t5_write, reg_t6_write, reg_t7_write, reg_t8_write,
       reg_t9_write, reg_v0_write, reg_v1_write, reg_zero_write;
  wire [31:0] multiplexer_1_out, multiplexer_2_out, multiplexer_3_out, multiplexer_4_out, multiplexer_5_out,
       multiplexer_6_out, multiplexer_7_out, multiplexer_8_out, multiplexer_9_out, multiplexer_10_out,
       multiplexer_11_out, multiplexer_12_out, multiplexer_13_out, multiplexer_14_out, multiplexer_15_out,
       multiplexer_16_out, multiplexer_17_out, multiplexer_18_out, multiplexer_19_out, multiplexer_20_out,
       multiplexer_21_out, multiplexer_22_out, multiplexer_23_out, multiplexer_24_out, multiplexer_25_out,
       multiplexer_26_out, multiplexer_27_out, multiplexer_28_out, multiplexer_29_out, multiplexer_30_out,
       multiplexer_31_out, multiplexer_32_out, reg_a0_out, reg_a1_out, reg_a2_out, reg_a3_out, reg_at_out,
       reg_fp_out, reg_gp_ou, reg_k0_out, reg_k1_out, reg_ra_out, reg_s4_out, reg_s5_out, reg_s6_out,
       reg_s7_out, reg_sp_out, reg_t0_out, reg_t1_out, reg_t2_out, reg_t3_out, reg_t4_out, reg_t5_out,
       reg_t6_out, reg_t7_out, reg_t8_out, reg_t9_out, reg_v0_out, reg_v1_out, reg_zero_out;

  Demultiplexer #(.select(5)) demultiplexer_1 (
    .out0(reg_zero_write), .out1(reg_at_write), .out2(reg_v0_write), .out3(reg_v1_write),
    .out4(reg_a0_write), .out5(reg_a1_write), .out6(reg_a2_write), .out7(reg_a3_write), .out8(reg_t0_write),
    .out9(reg_t1_write), .out10(reg_t2_write), .out11(reg_t3_write), .out12(reg_t4_write),
    .out13(reg_t5_write), .out14(reg_t6_write), .out15(reg_t7_write), .out16(reg_s0_write),
    .out17(reg_s1_write), .out18(reg_s2_write), .out19(reg_s3_write), .out20(reg_s4_write),
    .out21(reg_s5_write), .out22(reg_s6_write), .out23(reg_s7_write), .out24(reg_t8_write),
    .out25(reg_t9_write), .out26(reg_k0_write), .out27(reg_k1_write), .out28(reg_gp_write),
    .out29(reg_sp_write), .out30(reg_fp_write), .out31(reg_ra_write), .in(Write_Enable), .sel(Write_Register));  // open: en
  Multiplexer #(.width(32)) multiplexer_1 (
    .in0(reg_zero_out), .in1({32{1'b0}}), .out(multiplexer_1_out), .sel(reg_zero_write));  // open: en
  Multiplexer #(.width(32)) multiplexer_2 (
    .in0(reg_at_out), .in1(Write_Data), .out(multiplexer_2_out), .sel(reg_at_write));  // open: en
  Multiplexer #(.width(32)) multiplexer_3 (
    .in0(reg_v0_out), .in1(Write_Data), .out(multiplexer_3_out), .sel(reg_v0_write));  // open: en
  Multiplexer #(.width(32)) multiplexer_4 (
    .in0(reg_v1_out), .in1(Write_Data), .out(multiplexer_4_out), .sel(reg_v1_write));  // open: en
  Multiplexer #(.width(32)) multiplexer_5 (
    .in0(reg_a0_out), .in1(Write_Data), .out(multiplexer_5_out), .sel(reg_a0_write));  // open: en
  Multiplexer #(.width(32)) multiplexer_6 (
    .in0(reg_a1_out), .in1(Write_Data), .out(multiplexer_6_out), .sel(reg_a1_write));  // open: en
  Multiplexer #(.width(32)) multiplexer_7 (
    .in0(reg_a2_out), .in1(Write_Data), .out(multiplexer_7_out), .sel(reg_a2_write));  // open: en
  Multiplexer #(.width(32)) multiplexer_8 (
    .in0(reg_a3_out), .in1(Write_Data), .out(multiplexer_8_out), .sel(reg_a3_write));  // open: en
  Multiplexer #(.width(32)) multiplexer_9 (
    .in0(reg_t0_out), .in1(Write_Data), .out(multiplexer_9_out), .sel(reg_t0_write));  // open: en
  Multiplexer #(.width(32)) multiplexer_10 (
    .in0(reg_t1_out), .in1(Write_Data), .out(multiplexer_10_out), .sel(reg_t1_write));  // open: en
  Multiplexer #(.width(32)) multiplexer_11 (
    .in0(reg_t2_out), .in1(Write_Data), .out(multiplexer_11_out), .sel(reg_t2_write));  // open: en
  Multiplexer #(.width(32)) multiplexer_12 (
    .in0(reg_t3_out), .in1(Write_Data), .out(multiplexer_12_out), .sel(reg_t3_write));  // open: en
  Multiplexer #(.width(32)) multiplexer_13 (
    .in0(reg_t4_out), .in1(Write_Data), .out(multiplexer_13_out), .sel(reg_t4_write));  // open: en
  Multiplexer #(.width(32)) multiplexer_14 (
    .in0(reg_t5_out), .in1(Write_Data), .out(multiplexer_14_out), .sel(reg_t5_write));  // open: en
  Multiplexer #(.width(32)) multiplexer_15 (
    .in0(reg_t6_out), .in1(Write_Data), .out(multiplexer_15_out), .sel(reg_t6_write));  // open: en
  Multiplexer #(.width(32)) multiplexer_16 (
    .in0(reg_t7_out), .in1(Write_Data), .out(multiplexer_16_out), .sel(reg_t7_write));  // open: en
  Multiplexer #(.width(32)) multiplexer_17 (
    .in0(s0_Value), .in1(Write_Data), .out(multiplexer_17_out), .sel(reg_s0_write));  // open: en
  Multiplexer #(.width(32)) multiplexer_18 (
    .in0(s1_Value), .in1(Write_Data), .out(multiplexer_18_out), .sel(reg_s1_write));  // open: en
  Multiplexer #(.width(32)) multiplexer_19 (
    .in0(s2_Value), .in1(Write_Data), .out(multiplexer_19_out), .sel(reg_s2_write));  // open: en
  Multiplexer #(.width(32)) multiplexer_20 (
    .in0(ra_Value), .in1(Write_Data), .out(multiplexer_20_out), .sel(reg_s3_write));  // open: en
  Multiplexer #(.width(32)) multiplexer_21 (
    .in0(reg_s4_out), .in1(Write_Data), .out(multiplexer_21_out), .sel(reg_s4_write));  // open: en
  Multiplexer #(.width(32)) multiplexer_22 (
    .in0(reg_s5_out), .in1(Write_Data), .out(multiplexer_22_out), .sel(reg_s5_write));  // open: en
  Multiplexer #(.width(32)) multiplexer_23 (
    .in0(reg_s6_out), .in1(Write_Data), .out(multiplexer_23_out), .sel(reg_s6_write));  // open: en
  Multiplexer #(.width(32)) multiplexer_24 (
    .in0(reg_s7_out), .in1(Write_Data), .out(multiplexer_24_out), .sel(reg_s7_write));  // open: en
  Multiplexer #(.width(32)) multiplexer_25 (
    .in0(reg_t8_out), .in1(Write_Data), .out(multiplexer_25_out), .sel(reg_t8_write));  // open: en
  Multiplexer #(.width(32)) multiplexer_26 (
    .in0(reg_t9_out), .in1(Write_Data), .out(multiplexer_26_out), .sel(reg_t9_write));  // open: en
  Multiplexer #(.width(32)) multiplexer_27 (
    .in0(reg_k0_out), .in1(Write_Data), .out(multiplexer_27_out), .sel(reg_k0_write));  // open: en
  Multiplexer #(.width(32)) multiplexer_28 (
    .in0(reg_k1_out), .in1(Write_Data), .out(multiplexer_28_out), .sel(reg_k1_write));  // open: en
  Multiplexer #(.width(32)) multiplexer_29 (
    .in0(reg_gp_ou), .in1(Write_Data), .out(multiplexer_29_out), .sel(reg_gp_write));  // open: en
  Multiplexer #(.width(32)) multiplexer_30 (
    .in0(reg_sp_out), .in1(Write_Data), .out(multiplexer_30_out), .sel(reg_sp_write));  // open: en
  Multiplexer #(.width(32)) multiplexer_31 (
    .in0(reg_fp_out), .in1(Write_Data), .out(multiplexer_31_out), .sel(reg_fp_write));  // open: en
  Multiplexer #(.width(32)) multiplexer_32 (
    .in0(reg_ra_out), .in1(Write_Data), .out(multiplexer_32_out), .sel(reg_ra_write));  // open: en
  Register #(.width(32)) register_1 (.D(multiplexer_1_out), .Q(reg_zero_out), .clk(Clock));  // open: en, clr
  Register #(.width(32)) register_2 (.D(multiplexer_2_out), .Q(reg_at_out), .clk(Clock));  // open: en, clr
  Register #(.width(32)) register_3 (.D(multiplexer_3_out), .Q(reg_v0_out), .clk(Clock));  // open: en, clr
  Register #(.width(32)) register_4 (.D(multiplexer_4_out), .Q(reg_v1_out), .clk(Clock));  // open: en, clr
  Register #(.width(32)) register_5 (.D(multiplexer_5_out), .Q(reg_a0_out), .clk(Clock));  // open: en, clr
  Register #(.width(32)) register_6 (.D(multiplexer_6_out), .Q(reg_a1_out), .clk(Clock));  // open: en, clr
  Register #(.width(32)) register_7 (.D(multiplexer_7_out), .Q(reg_a2_out), .clk(Clock));  // open: en, clr
  Register #(.width(32)) register_8 (.D(multiplexer_8_out), .Q(reg_a3_out), .clk(Clock));  // open: en, clr
  Register #(.width(32)) register_9 (.D(multiplexer_9_out), .Q(reg_t0_out), .clk(Clock));  // open: en, clr
  Register #(.width(32)) register_10 (.D(multiplexer_10_out), .Q(reg_t1_out), .clk(Clock));  // open: en, clr
  Register #(.width(32)) register_11 (.D(multiplexer_11_out), .Q(reg_t2_out), .clk(Clock));  // open: en, clr
  Register #(.width(32)) register_12 (.D(multiplexer_12_out), .Q(reg_t3_out), .clk(Clock));  // open: en, clr
  Register #(.width(32)) register_13 (.D(multiplexer_13_out), .Q(reg_t4_out), .clk(Clock));  // open: en, clr
  Register #(.width(32)) register_14 (.D(multiplexer_14_out), .Q(reg_t5_out), .clk(Clock));  // open: en, clr
  Register #(.width(32)) register_15 (.D(multiplexer_15_out), .Q(reg_t6_out), .clk(Clock));  // open: en, clr
  Register #(.width(32)) register_16 (.D(multiplexer_16_out), .Q(reg_t7_out), .clk(Clock));  // open: en, clr
  Register #(.width(32)) register_17 (.D(multiplexer_17_out), .Q(s0_Value), .clk(Clock));  // open: en, clr
  Register #(.width(32)) register_18 (.D(multiplexer_18_out), .Q(s1_Value), .clk(Clock));  // open: en, clr
  Register #(.width(32)) register_19 (.D(multiplexer_19_out), .Q(s2_Value), .clk(Clock));  // open: en, clr
  Register #(.width(32)) register_20 (.D(multiplexer_20_out), .Q(ra_Value), .clk(Clock));  // open: en, clr
  Register #(.width(32)) register_21 (.D(multiplexer_21_out), .Q(reg_s4_out), .clk(Clock));  // open: en, clr
  Register #(.width(32)) register_22 (.D(multiplexer_22_out), .Q(reg_s5_out), .clk(Clock));  // open: en, clr
  Register #(.width(32)) register_23 (.D(multiplexer_23_out), .Q(reg_s6_out), .clk(Clock));  // open: en, clr
  Register #(.width(32)) register_24 (.D(multiplexer_24_out), .Q(reg_s7_out), .clk(Clock));  // open: en, clr
  Register #(.width(32)) register_25 (.D(multiplexer_25_out), .Q(reg_t8_out), .clk(Clock));  // open: en, clr
  Register #(.width(32)) register_26 (.D(multiplexer_26_out), .Q(reg_t9_out), .clk(Clock));  // open: en, clr
  Register #(.width(32)) register_27 (.D(multiplexer_27_out), .Q(reg_k0_out), .clk(Clock));  // open: en, clr
  Register #(.width(32)) register_28 (.D(multiplexer_28_out), .Q(reg_k1_out), .clk(Clock));  // open: en, clr
  Register #(.width(32)) register_29 (.D(multiplexer_29_out), .Q(reg_gp_ou), .clk(Clock));  // open: en, clr
  Register #(.width(32)) register_30 (.D(multiplexer_30_out), .Q(reg_sp_out), .clk(Clock));  // open: en, clr
  Register #(.width(32)) register_31 (.D(multiplexer_31_out), .Q(reg_fp_out), .clk(Clock));  // open: en, clr
  Register #(.width(32)) register_32 (.D(multiplexer_32_out), .Q(reg_ra_out), .clk(Clock));  // open: en, clr
  Multiplexer #(.select(5), .width(32)) multiplexer_33 (
    .in0(reg_zero_out), .in1(reg_at_out), .in2(reg_v0_out), .in3(reg_v1_out), .in4(reg_a0_out),
    .in5(reg_a1_out), .in6(reg_a2_out), .in7(reg_a3_out), .in8(reg_t0_out), .in9(reg_t1_out),
    .in10(reg_t2_out), .in11(reg_t3_out), .in12(reg_t4_out), .in13(reg_t5_out), .in14(reg_t6_out),
    .in15(reg_t7_out), .in16(s0_Value), .in17(s1_Value), .in18(s2_Value), .in19(ra_Value), .in20(reg_s4_out),
    .in21(reg_s5_out), .in22(reg_s6_out), .in23(reg_s7_out), .in24(reg_t8_out), .in25(reg_t9_out),
    .in26(reg_k0_out), .in27(reg_k1_out), .in28(reg_gp_ou), .in29(reg_sp_out), .in30(reg_fp_out),
    .in31(reg_ra_out), .out(Read_Data_1), .sel(Read_Register_1));  // open: en
  Multiplexer #(.select(5), .width(32)) multiplexer_34 (
    .in0(reg_zero_out), .in1(reg_at_out), .in2(reg_v0_out), .in3(reg_v1_out), .in4(reg_a0_out),
    .in5(reg_a1_out), .in6(reg_a2_out), .in7(reg_a3_out), .in8(reg_t0_out), .in9(reg_t1_out),
    .in10(reg_t2_out), .in11(reg_t3_out), .in12(reg_t4_out), .in13(reg_t5_out), .in14(reg_t6_out),
    .in15(reg_t7_out), .in16(s0_Value), .in17(s1_Value), .in18(s2_Value), .in19(ra_Value), .in20(reg_s4_out),
    .in21(reg_s5_out), .in22(reg_s6_out), .in23(reg_s7_out), .in24(reg_t8_out), .in25(reg_t9_out),
    .in26(reg_k0_out), .in27(reg_k1_out), .in28(reg_gp_ou), .in29(reg_sp_out), .in30(reg_fp_out),
    .in31(reg_ra_out), .out(Read_Data_2), .sel(Read_Register_2));  // open: en

  // Other names for the same wires on the sheet: clk = Clock; read_data1[31:0] = Read_Data_1;
  //   read_data2[31:0] = Read_Data_2; read_reg1[4:0] = Read_Register_1; read_reg2[4:0] = Read_Register_2;
  //   reg_s0_out[31:0] = s0_Value; s0_test[31:0] = s0_Value; reg_s1_out[31:0] = s1_Value; s1_test[31:0] = s1_Value;
  //   reg_s2_out[31:0] = s2_Value; s2_test[31:0] = s2_Value; reg_s3_out[31:0] = ra_Value; s3_test[31:0] = ra_Value;
  //   write_en = Write_Enable; write_reg[4:0] = Write_Register

  // Notes on the sheet:
  //   INPUTS to your circuit
  //   DON'T CHANGE THE LOCATIONS OF THE INPUTS AND OUTPUTS!
  //   These are DEBUG/TEST outputs from your circuit.
  //   OUTPUTS from your circuit
endmodule
